# Fritzing sketch Robot (saved by Fritzing 0.8.7b)
breadboards: 1

parts:
  Part1 = SRF05 Ultrasonic Rangefinder
  S1 = H-Bridge with L298N
  Part2 = Arduino Uno (Rev3)
  M2 = DC Motor
  M3 = DC Motor
  J1 = Basic Servo
  Part3 = IR Receiver Breakout [package=PCB]
  LED3 = RGB LED (com. cathode, rbg) [package="5 mm [THT]"]
  VCC1 = Battery block 9V
  S2 = SWITCH-DPDT [package=os]
  R1 = Resistor [tolerance=±5% resistance=220 package=THT]
  R2 = Resistor [tolerance=±5% resistance=220 package=THT]
  R3 = Resistor [tolerance=±5% resistance=220 package=THT]

nets:
  VCC: Part1.VCC, Part2.D4, J1.vcc, Part3.OUT, Part3.VCC
  N1: Part1.Trig, Part2.D9_PWM
  N2: Part1.Echo, Part2.D8
  GND: Part1.GND, S1.GND, Part2.GND, J1.gnd, Part3.GND, LED3.common_cathode, VCC1.-
  N3: S1.12V, S2.6
  5V: S1.5V, Part2.VIN
  N4: S1.ENA, Part2.D11_PWM/MOSI
  N5: S1.IN1, Part2.A1
  N6: S1.IN2, Part2.A2
  N7: S1.IN3, Part2.A3
  N8: S1.IN4, Part2.A4/SDA
  N9: S1.ENB, Part2.D3_PWM
  N10: S1.M1-01, M3.pin_2
  N11: S1.M1-02, M3.pin_1
  N12: S1.M2-01, M2.pin_1
  N13: S1.M2-02, M2.pin_2
  N14: Part2.D10_PWM/SS, J1.pulse
  N15: Part2.D5_PWM, R2.Pin_0
  N16: Part2.D6_PWM, R3.Pin_0
  N17: Part2.D7, R1.Pin_0
  N18: LED3.red_anode, R1.Pin_1
  N19: LED3.blue_anode, R2.Pin_1
  N20: LED3.green_anode, R3.Pin_1
  N21: VCC1.+, S2.1

custom parts:
  H-Bridge with L298N: h-bridge
